# Fritzing sketch CouvertureChauffanteSchema3 (saved by Fritzing 0.9.4)
circuit board: 13.6286cm x 8.3008cm
breadboards: 2

parts:
  LCD_16x4 = LCD screen
  R1 = Resistor [tolerance=±5% resistance=220 package=THT]
  EEPROM = 24LC128 [package=THT]
  R5 = Resistor [tolerance=±5% resistance=10k package=THT]
  R6 = Resistor [tolerance=±5% resistance=10k package=THT]
  R11 = Resistor [tolerance=±5% resistance=10k package=THT]
  R12 = Resistor [tolerance=±5% resistance=10k package=THT]
  R13 = Resistor [tolerance=±5% resistance=10k package=THT]
  R14 = Resistor [tolerance=±5% resistance=10k package=THT]
  thRL+ = female pin header, 1 pin [form="♀ (female)"]
  thFR+ = female pin header, 1 pin [form="♀ (female)"]
  thFL+ = female pin header, 1 pin [form="♀ (female)"]
  thFLS = female pin header, 1 pin [form="♀ (female)"]
  thFRS = female pin header, 1 pin [form="♀ (female)"]
  thRLS = female pin header, 1 pin [form="♀ (female)"]
  thRRS = female pin header, 1 pin [form="♀ (female)"]
  pwFL+ = female pin header, 1 pin [form="♀ (female)"]
  pwRL+ = female pin header, 1 pin [form="♀ (female)"]
  pwFR- = female pin header, 1 pin [form="♀ (female)"]
  pwRL- = female pin header, 1 pin [form="♀ (female)"]
  pwFR+ = female pin header, 1 pin [form="♀ (female)"]
  pwRR- = female pin header, 1 pin [form="♀ (female)"]
  pwRR+ = female pin header, 1 pin [form="♀ (female)"]
  pwFL- = female pin header, 1 pin [form="♀ (female)"]
  trFL = NPN-Transistor [package="TO92 [THT]"]
  trFR = NPN-Transistor [package="TO92 [THT]"]
  thRR+ = female pin header, 1 pin [form="♀ (female)"]
  trRR = NPN-Transistor [package="TO92 [THT]"]
  trRL = NPN-Transistor [package="TO92 [THT]"]
  R15 = Resistor [tolerance=±5% resistance=1k package=THT]
  R16 = Resistor [tolerance=±5% resistance=1k package=THT]
  R17 = Resistor [tolerance=±5% resistance=1k package=THT]
  R18 = Resistor [tolerance=±5% resistance=1k package=THT]
  12V = Screw terminal - 2 pins [package=THT]
  ArduinoNano = Arduino Nano (Rev3.0)
  RPshBck = Resistor [tolerance=±5% resistance=10k package=THT]
  PshDwn = Pushbutton [package="[THT]"]
  PshUp = Pushbutton [package="[THT]"]
  PshVal = Pushbutton [package="[THT]"]
  PshBck = Pushbutton [package="[THT]"]
  RPshVal = Resistor [tolerance=±5% resistance=1k package=THT]
  RPshUp = Resistor [tolerance=±5% resistance=1k package=THT]
  RPshDwn = Resistor [tolerance=±5% resistance=1k package=THT]

nets:
  VSS: LCD_16x4.VSS, LCD_16x4.R/W, LCD_16x4.LED-, EEPROM.0V, EEPROM.WP_-_Write_Protect, R11.Pin_1, R12.Pin_1, R13.Pin_1, R14.Pin_1, pwFL+.pin1, pwRL+.pin1, pwFR-.pin1, pwRL-.pin1, pwFR+.pin1, pwRR-.pin1, pwRR+.pin1, pwFL-.pin1, trFL.C, trFR.C, trRR.C, trRL.C, 12V.pin1, ArduinoNano.GND, PshDwn.Pin_1, PshDwn.Pin_2, PshUp.Pin_1, PshUp.Pin_2, PshVal.Pin_1, PshVal.Pin_2, PshBck.Pin_1, PshBck.Pin_2
  VDD: LCD_16x4.VDD, R1.Pin_1, EEPROM.+V, R5.Pin_0, R6.Pin_0, thRL+.pin1, thFR+.pin1, thFL+.pin1, thRR+.pin1, ArduinoNano.5V, RPshBck.Pin_0
  N1: LCD_16x4.V0, ArduinoNano.D6
  N2: LCD_16x4.RS, ArduinoNano.D12/MISO
  N3: LCD_16x4.E, ArduinoNano.D11/MOSI
  N4: LCD_16x4.DB4, ArduinoNano.D5
  N5: LCD_16x4.DB5, ArduinoNano.D4
  N6: LCD_16x4.DB6, ArduinoNano.D3
  N7: LCD_16x4.DB7, ArduinoNano.D2
  N8: LCD_16x4.LED+, R1.Pin_0
  N9: EEPROM.SDA_-_I2C_Data, R6.Pin_1, ArduinoNano.A4
  N10: EEPROM.SCL_-_I2C_Clock, R5.Pin_1, ArduinoNano.A5
  N11: R11.Pin_0, thFLS.pin1, ArduinoNano.A0
  N12: R12.Pin_0, thFRS.pin1, ArduinoNano.A1
  N13: R13.Pin_0, thRLS.pin1, ArduinoNano.A3
  N14: R14.Pin_0, thRRS.pin1, ArduinoNano.A2
  N15: trFL.E, trFR.E, trRR.E, trRL.E, 12V.pin2, ArduinoNano.VIN
  N16: trFL.B, R15.Pin_0
  N17: trFR.B, R16.Pin_0
  N18: trRR.B, R18.Pin_0
  N19: trRL.B, R17.Pin_0
  N20: R15.Pin_1, ArduinoNano.D9
  N21: R16.Pin_1, ArduinoNano.D10
  N22: R17.Pin_1, ArduinoNano.D7
  N23: R18.Pin_1, ArduinoNano.D8
  N24: ArduinoNano.A6, RPshBck.Pin_1, PshBck.Pin_3, PshBck.Pin_4, RPshVal.Pin_0
  N25: PshDwn.Pin_3, PshDwn.Pin_4, RPshDwn.Pin_1
  N26: PshUp.Pin_3, PshUp.Pin_4, RPshUp.Pin_1, RPshDwn.Pin_0
  N27: PshVal.Pin_3, PshVal.Pin_4, RPshVal.Pin_1, RPshUp.Pin_0
