# Fritzing sketch CouvertureChauffanteSchema_NewGen (saved by Fritzing 0.9.4)
circuit board: 3.16985cm x 3.62778cm
circuit board: 13.3497cm x 4.74365cm
breadboards: 2

parts:
  LCD_16x4 = LCD screen
  R1 = Resistor [tolerance=±5% resistance=220 package=THT]
  EEPROM = 24LC128 [package=THT]
  R5 = Resistor [tolerance=±5% resistance=10k package=THT]
  R6 = Resistor [tolerance=±5% resistance=10k package=THT]
  R11 = Resistor [tolerance=±5% resistance=10k package=THT]
  R12 = Resistor [tolerance=±5% resistance=10k package=THT]
  R13 = Resistor [tolerance=±5% resistance=10k package=THT]
  R14 = Resistor [tolerance=±5% resistance=10k package=THT]
  trFL = NPN-Transistor [package="TO92 [THT]"]
  trFR = NPN-Transistor [package="TO92 [THT]"]
  trRR = NPN-Transistor [package="TO92 [THT]"]
  trRL = NPN-Transistor [package="TO92 [THT]"]
  R15 = Resistor [tolerance=±5% resistance=1k package=THT]
  R16 = Resistor [tolerance=±5% resistance=1k package=THT]
  R17 = Resistor [tolerance=±5% resistance=1k package=THT]
  R18 = Resistor [tolerance=±5% resistance=1k package=THT]
  ArduinoNano = Arduino Nano (Rev3.0)
  RPshBck = Resistor [tolerance=±5% resistance=10k package=THT]
  PshDwn = Pushbutton [package="[THT]"]
  PshUp = Pushbutton [package="[THT]"]
  PshVal = Pushbutton [package="[THT]"]
  PshBck = Pushbutton [package="[THT]"]
  RPshVal = Resistor [tolerance=±5% resistance=1k package=THT]
  RPshUp = Resistor [tolerance=±5% resistance=1k package=THT]
  RPshDwn = Resistor [tolerance=±5% resistance=1k package=THT]
  tRL+ = female pin header, 1 pin [form="♀ (female)"]
  pRL+ = female pin header, 1 pin [form="♀ (female)"]
  pRR+ = female pin header, 1 pin [form="♀ (female)"]
  tRR+ = female pin header, 1 pin [form="♀ (female)"]
  pRR- = female pin header, 1 pin [form="♀ (female)"]
  tRRs = female pin header, 1 pin [form="♀ (female)"]
  tRLs = female pin header, 1 pin [form="♀ (female)"]
  pRL- = female pin header, 1 pin [form="♀ (female)"]
  pFL- = female pin header, 1 pin [form="♀ (female)"]
  tFL+ = female pin header, 1 pin [form="♀ (female)"]
  tFLs = female pin header, 1 pin [form="♀ (female)"]
  pFL+ = female pin header, 1 pin [form="♀ (female)"]
  pFR+ = female pin header, 1 pin [form="♀ (female)"]
  tFRs = female pin header, 1 pin [form="♀ (female)"]
  pFR- = female pin header, 1 pin [form="♀ (female)"]
  tFR+ = female pin header, 1 pin [form="♀ (female)"]
  12V = Screw terminal - 2 pins [package=THT]
  J1 = female pin header, 2 pins [form="♀ (female)"]
  LED1 = smd LED [color="Red (633nm)" package="0603 [SMD]"]
  R19 = Resistor [tolerance=±5% resistance=10k package=THT]
  J2 = female pin header, 2 pins [form="♀ (female)"]
  J3 = Power Jack [package=power_jack_pth]  # not connected

nets:
  VSS: LCD_16x4.VSS, LCD_16x4.R/W, LCD_16x4.LED-, EEPROM.0V, EEPROM.WP_-_Write_Protect, R11.Pin_1, R12.Pin_1, R13.Pin_1, R14.Pin_1, trFL.C, trFR.C, trRR.C, trRL.C, ArduinoNano.GND, PshDwn.Pin_1, PshDwn.Pin_2, PshUp.Pin_1, PshUp.Pin_2, PshVal.Pin_1, PshVal.Pin_2, PshBck.Pin_1, PshBck.Pin_2, 12V.pin1, LED1.cathode, J2.pin2
  VDD: LCD_16x4.VDD, R1.Pin_1, EEPROM.+V, R5.Pin_0, R6.Pin_0, ArduinoNano.5V, RPshBck.Pin_0, tRL+.pin1, tRR+.pin1, tFL+.pin1, tFR+.pin1
  N1: LCD_16x4.V0, ArduinoNano.D6
  N2: LCD_16x4.RS, ArduinoNano.D12/MISO
  N3: LCD_16x4.E, ArduinoNano.D11/MOSI
  N4: LCD_16x4.DB4, ArduinoNano.D5
  N5: LCD_16x4.DB5, ArduinoNano.D4
  N6: LCD_16x4.DB6, ArduinoNano.D3
  N7: LCD_16x4.DB7, ArduinoNano.D2
  N8: LCD_16x4.LED+, R1.Pin_0
  N9: EEPROM.SDA_-_I2C_Data, R6.Pin_1, ArduinoNano.A4
  N10: EEPROM.SCL_-_I2C_Clock, R5.Pin_1, ArduinoNano.A5
  N11: R11.Pin_0, ArduinoNano.A1, tFLs.pin1
  N12: R12.Pin_0, ArduinoNano.A0, tFRs.pin1
  N13: R13.Pin_0, ArduinoNano.A3, tRLs.pin1
  N14: R14.Pin_0, ArduinoNano.A2, tRRs.pin1
  N15: trFL.E, pFL-.pin1
  N16: trFL.B, R15.Pin_0
  N17: trFR.E, pFR-.pin1
  N18: trFR.B, R16.Pin_0
  N19: trRR.E, pRR-.pin1
  N20: trRR.B, R18.Pin_0
  N21: trRL.E, pRL-.pin1
  N22: trRL.B, R17.Pin_0
  N23: R15.Pin_1, ArduinoNano.D9
  N24: R16.Pin_1, ArduinoNano.D10
  N25: R17.Pin_1, ArduinoNano.D7
  N26: R18.Pin_1, ArduinoNano.D8
  N27: ArduinoNano.VIN, J1.pin1
  N28: ArduinoNano.A6, RPshBck.Pin_1, PshBck.Pin_3, PshBck.Pin_4, RPshVal.Pin_0, J2.pin1
  N29: PshDwn.Pin_3, PshDwn.Pin_4, RPshDwn.Pin_1
  N30: PshUp.Pin_3, PshUp.Pin_4, RPshUp.Pin_1, RPshDwn.Pin_0
  N31: PshVal.Pin_3, PshVal.Pin_4, RPshVal.Pin_1, RPshUp.Pin_0
  N32: pRL+.pin1, pRR+.pin1, pFL+.pin1, pFR+.pin1, 12V.pin2, J1.pin2, R19.Pin_0
  N33: LED1.anode, R19.Pin_1
